// Logisim project LC-3.circ as structural Verilog: 21 circuits, main circuit main
module main (
  input  Reset,
  output out_2,
  output out_3,
  output out_4,
  output out_5,
  output out_6,
  output out_7,
  output out_8,
  output [15:0] out_9,
  output [15:0] out_10,
  output [15:0] out_11,
  output [15:0] out_12,
  output [15:0] out_13,
  output [15:0] out_14,
  output [15:0] out_15,
  output [15:0] out_16,
  output [15:0] out_17,
  output halt,
  output [15:0] out_19,
  output [15:0] out_20,
  output [15:0] out_21,
  output [15:0] out_22
);

  wire decodeir_1_doldi, decodeir_1_writereg, DoLDI, DoLDI2, getcst_1_usecst, not_1_out, or16_1_out_2,
       or16_2_out_2, ramctrl_1_memload, ramctrl_1_memstore;
  wire [1:0] getop_1_out_2;
  wire [2:0] nzp_1_nzp, RegIn_out_3;
  wire [15:0] addr2, alu_1_output, arg_1_out_5, arg_1_out_6, getcst_1_cst, multiplexer_1_out, RegIN,
       registres_1_out_sr1, registres_1_out_sr2;

  BiClock biclock_1 (.reset(Reset), .signal0(out_2), .signal1(out_3));
  RegPC regpc_1 (
    .H(out_3), .PC(out_9), .Reset(Reset), .IR(out_10), .R(registres_1_out_sr1), .TestNZP(out_5), .Jump(out_4));
  // Probe on out_9
  and and_1 (DoLDI2, out_6, decodeir_1_doldi, out_3);
  GetAddr getaddr_1 (.PC(out_9), .R(registres_1_out_sr1), .IR(out_10), .Addr(out_11), .Fetch(out_2));
  // Probe on out_11
  Multiplexer #(.width(16), .enable("false")) multiplexer_1 (
    .in0(out_11), .in1(addr2), .out(multiplexer_1_out), .sel(DoLDI2));
  // Probe on out_12
  LED led_1 (.in(out_6));
  RamCtrl ramctrl_1 (
    .Store(out_7), .Fetch(out_2), .Exec(out_3), .Load(out_6), .MemStore(ramctrl_1_memstore),
    .MemLoad(ramctrl_1_memload));
  LED led_2 (.in(out_7));
  and and_2 (DoLDI, decodeir_1_doldi, out_6, not_1_out);
  not not_1 (not_1_out, out_3);
  Register #(.width(16), .trigger("falling")) RegIR (.D(out_13), .Q(addr2), .clk(DoLDI));  // open: en, clr
  // Probe on out_13
  RAM #(.addrWidth(16), .dataWidth(16), .bus("separate")) ram_1 (
    .addr(multiplexer_1_out), .din(out_12), .data(out_13), .str(ramctrl_1_memstore),
    .clk(ramctrl_1_memstore), .ld(ramctrl_1_memload));  // open: sel, clr
  Register #(.width(16), .trigger("falling")) RegIR_2 (.D(out_13), .Q(out_10), .clk(out_2));  // open: en, clr
  DecodeIR decodeir_1 (
    .IR(out_10), .Jump(out_4), .WriteReg(decodeir_1_writereg), .Load(out_6), .Store(out_7),
    .DoLDI(decodeir_1_doldi));
  // Probe on RegIn_out_3
  // Probe on out_10[8:6]
  // Probe on out_10[2:0]
  RegIn u_RegIn (.in_1(out_10[11:9]), .in_2(out_10), .out_3(RegIn_out_3));
  // Probe on getcst_1_cst
  GetCst getcst_1 (.IR(out_10), .Cst(getcst_1_cst), .UseCst(getcst_1_usecst));
  GetOp getop_1 (.in_1(out_10), .out_2(getop_1_out_2));
  // Probe on getop_1_out_2
  and and_3 (out_8, decodeir_1_writereg, out_3);
  Registres registres_1 (
    .SR1(out_10[8:6]), .IN(RegIN), .SR2(out_10[2:0]), .WriteReg(out_8), .DR_SR(RegIn_out_3),
    .OUT_SR1(registres_1_out_sr1), .OUT_SR2(registres_1_out_sr2), .OUT_SR(out_12), .R0(out_14), .R1(out_15),
    .R2(out_16), .R3(out_17), .R4(out_19), .R5(out_20), .R6(out_21), .R7(out_22));
  Arg arg_1 (
    .PC(out_9), .IR(out_10), .ARG1(registres_1_out_sr1), .ARG2(registres_1_out_sr2), .out_5(arg_1_out_5),
    .out_6(arg_1_out_6));
  // Probe on arg_1_out_5
  ALU alu_1 (
    .UseCst(getcst_1_usecst), .e2(getop_1_out_2), .Input1(arg_1_out_5), .Input2(arg_1_out_6),
    .Cst(getcst_1_cst), .Output(alu_1_output));
  // Probe on arg_1_out_6
  // Probe on alu_1_output
  NZP nzp_1 (.RES(RegIN), .NZP(nzp_1_nzp), .IR(out_10), .TestNZP(out_5), .WriteReg(out_8));
  // Probe on nzp_1_nzp
  Or16 or16_1 (.in_1(out_10), .out_2(or16_1_out_2));
  Or16 or16_2 (.in_1(out_9), .out_2(or16_2_out_2));
  // Probe on out_14
  // Probe on out_15
  // Probe on out_16
  // Probe on out_17
  // Probe on out_19
  // Probe on out_20
  // Probe on out_21
  // Probe on out_22
  and and_4 (halt, ~or16_1_out_2, or16_2_out_2);  // AND_Gate
  Multiplexer #(.width(16), .enable("false")) multiplexer_2 (
    .in0(alu_1_output), .in1(out_13), .out(RegIN), .sel(out_6));
  // Probe on RegIN

  // Other names for the same wires on the sheet: Addr[15:0] = out_11; Condition = out_5; Exec = out_3; Fetch = out_2;
  //   IR[15:0] = out_10; JumpInstr = out_4; Load = out_6; MemIN[15:0] = out_12; MemOUT[15:0] = out_13;
  //   PC[15:0] = out_9; R0[15:0] = out_14; R1[15:0] = out_15; R2[15:0] = out_16; R3[15:0] = out_17; R4[15:0] = out_19;
  //   R5[15:0] = out_20; R6[15:0] = out_21; R7[15:0] = out_22; Store = out_7; WriteReg = out_8

  // Notes on the sheet:
  //   R
  //   IR
  //   R
  //   IR
  //   RAM
  //   Traces (NE PAS MODIFIER)______________________________________________________________________________________________________
  //   GetOp
  //   Arret des traces au 1er NOP
endmodule

module ALU (
  input  [15:0] Input1,
  input  [15:0] Input2,
  input  [15:0] Cst,
  input  UseCst,
  input  [1:0] e2,
  output [15:0] Output
);

  wire [15:0] adder_1_out, and_1_out, multiplexer_1_out, xxor_1_out_3;

  Multiplexer #(.width(16), .enable("false")) multiplexer_1 (
    .in0(Input2), .in1(Cst), .out(multiplexer_1_out), .sel(UseCst));
  Adder #(.width(16)) adder_1 (.a(multiplexer_1_out), .b(Input1), .out(adder_1_out));  // open: cin, cout
  assign and_1_out = Input1 & multiplexer_1_out;  // AND_Gate and_1, 16 bits wide
  Multiplexer #(.select(2), .width(16), .enable("false")) multiplexer_2 (
    .in0(adder_1_out), .in1(and_1_out), .in2(xxor_1_out_3), .out(Output), .sel(e2));  // open: in3
  // Probe on xxor_1_out_3
  XXor xxor_1 (.B(Input1), .A(multiplexer_1_out), .out_3(xxor_1_out_3));
endmodule

module BiClock (
  input  reset,
  output signal0,
  output signal1
);

  wire and_1_out, horloge_out, not_1_out, register_1_q;

  Clock horloge (.out(horloge_out));
  not not_1 (not_1_out, register_1_q);
  Register #(.width(1), .trigger("falling")) register_1 (
    .D(not_1_out), .Q(register_1_q), .clk(horloge_out), .clr(reset));  // open: en
  and and_1 (and_1_out, horloge_out, ~reset);  // AND_Gate
  and and_2 (signal0, ~register_1_q, and_1_out);  // AND_Gate
  and and_3 (signal1, register_1_q, and_1_out);

  // Notes on the sheet:
  //   Ce module divise une horloge en deux sous-horloges alternées
  //   Chronogrammes :
  //   horloge: 0101010101 signal0: 0100010001 signal1: 000100010
  //   registre 1-bit
  //   Enable
  //   select : 0 / 1
endmodule

module DecodeIR (
  input  [15:0] IR,
  output Jump,
  output Load,
  output Store,
  output WriteReg,
  output DoLDI
);

  wire decodeop_1_add, decodeop_1_and, decodeop_1_br, decodeop_1_jmp, decodeop_1_jsr, decodeop_1_jsrr,
       decodeop_1_ld, decodeop_1_ldi, decodeop_1_ldr, decodeop_1_lea, decodeop_1_not, decodeop_1_st,
       decodeop_1_sti, decodeop_1_str, or_2_out, or_4_out;

  DecodeOp decodeop_1 (
    .in_1(IR), .NOT(decodeop_1_not), .AND(decodeop_1_and), .ADD(decodeop_1_add), .LEA(decodeop_1_lea),
    .ST(decodeop_1_st), .STR(decodeop_1_str), .STI(decodeop_1_sti), .LD(decodeop_1_ld), .LDR(decodeop_1_ldr),
    .LDI(decodeop_1_ldi), .BR(decodeop_1_br), .JMP(decodeop_1_jmp), .JSR(decodeop_1_jsr),
    .JSRR(decodeop_1_jsrr));
  or or_1 (DoLDI, decodeop_1_sti, decodeop_1_ldi);
  or or_2 (or_2_out, decodeop_1_jsrr, decodeop_1_ldr, decodeop_1_ld, decodeop_1_lea, decodeop_1_and, decodeop_1_add, decodeop_1_jsr, decodeop_1_not);
  or or_3 (WriteReg, or_2_out, decodeop_1_ldi);
  or or_4 (or_4_out, decodeop_1_not, decodeop_1_and, decodeop_1_add);
  // Probe on or_4_out
  or or_5 (Jump, decodeop_1_br, decodeop_1_jsrr, decodeop_1_jmp, decodeop_1_jsr);
  or or_6 (Load, decodeop_1_ld, decodeop_1_ldr, decodeop_1_sti, decodeop_1_ldi);
  or or_7 (Store, decodeop_1_st, decodeop_1_str);

  // Notes on the sheet:
  //   Types d'instructions
  //   (toujours oui pour l'instant)
  //   (toujours arith pour l'instant)
  //   Instruction modifiant les registres
endmodule

module GetAddr (
  input  [15:0] PC,
  input  Fetch,
  input  [15:0] R,
  input  [15:0] IR,
  output [15:0] Addr
);

  wire decodeop_1_ld, decodeop_1_ldi, decodeop_1_ldr, decodeop_1_st, decodeop_1_sti, decodeop_1_str,
       or_1_out, or_2_out, or_3_out;
  wire [15:0] adder_1_out, adder_2_out, bit_extender_1_out, bit_extender_2_out, multiplexer_2_out,
       multiplexer_3_out;

  DecodeOp decodeop_1 (
    .in_1(IR), .ST(decodeop_1_st), .STR(decodeop_1_str), .STI(decodeop_1_sti), .LD(decodeop_1_ld),
    .LDR(decodeop_1_ldr), .LDI(decodeop_1_ldi));  // open: NOT, AND, ADD, LEA, BR, JMP, JSR, JSRR
  or or_1 (or_1_out, decodeop_1_sti, decodeop_1_st, decodeop_1_ld, decodeop_1_ldi);
  or or_2 (or_2_out, decodeop_1_str, decodeop_1_ldr);
  assign bit_extender_1_out = {{7{IR[8]}}, IR[8:0]};  // Bit_Extender bit_extender_1
  assign bit_extender_2_out = {{10{IR[5]}}, IR[5:0]};  // Bit_Extender bit_extender_2
  Adder #(.width(16)) adder_1 (.a(bit_extender_1_out), .b(PC), .out(adder_1_out), .cin(1'b1));  // open: cout
  Adder #(.width(16)) adder_2 (.a(bit_extender_2_out), .b(R), .out(adder_2_out));  // open: cin, cout
  Multiplexer #(.width(16), .enable("false")) multiplexer_1 (
    .in0(multiplexer_3_out), .in1(PC), .out(Addr), .sel(Fetch));
  Multiplexer #(.width(16), .enable("false")) multiplexer_2 (
    .in0(adder_1_out), .in1(adder_2_out), .out(multiplexer_2_out), .sel(or_2_out));
  or or_3 (or_3_out, or_1_out, or_2_out);
  Multiplexer #(.width(16), .enable("false")) multiplexer_3 (
    .in0(PC), .in1(multiplexer_2_out), .out(multiplexer_3_out), .sel(or_3_out));
endmodule

module GetCst (
  input  [15:0] IR,
  output [15:0] Cst,
  output UseCst
);

  assign Cst = {{11{IR[4]}}, IR[4:0]};  // Bit_Extender bit_extender_1

  assign UseCst = IR[5];
endmodule

module NZP (
  input  [15:0] RES,
  input  [15:0] IR,
  input  WriteReg,
  output [2:0] NZP,
  output TestNZP
);

  wire and_1_out, and_2_out, and_3_out, and_4_out, decodeop_1_jsr, decodeop_1_jsrr, not_1_out, or_1_out,
       or_2_out, or_3_out;
  wire [1:0] not_3_out;

  DecodeOp decodeop_1 (
    .in_1(IR), .JSR(decodeop_1_jsr), .JSRR(decodeop_1_jsrr));  // open: NOT, AND, ADD, LEA, ST, STR, STI, LD, LDR, LDI, BR, JMP
  not not_1 (not_1_out, or_1_out);
  and and_1 (and_1_out, not_1_out, WriteReg);
  or or_1 (or_1_out, decodeop_1_jsr, decodeop_1_jsrr);
  or or_2 (or_2_out, RES[0], RES[1], RES[2], RES[3], RES[4], RES[5], RES[6], RES[7], RES[8], RES[9], RES[10], RES[11], RES[12], RES[13], RES[14], RES[15]);
  not not_2 (not_3_out[1], or_2_out);
  or or_3 (or_3_out, not_3_out[1], RES[15]);
  not not_3 (not_3_out[0], or_3_out);
  and and_2 (and_2_out, NZP[0], IR[9]);
  and and_3 (and_3_out, NZP[1], IR[10]);
  and and_4 (and_4_out, NZP[2], IR[11]);
  or or_4 (TestNZP, and_2_out, and_3_out, and_4_out);
  Register #(.width(3)) register_1 (.D({RES[15], not_3_out}), .Q(NZP), .clk(and_1_out));  // open: en, clr

  // Notes on the sheet:
  //   P
  //   Z
  //   N
endmodule

// Off6
module Offset6 (
  input  [15:0] IR,
  output [15:0] Off6
);

  assign Off6 = {{10{IR[5]}}, IR[5:0]};  // Bit_Extender bit_extender_1
endmodule

// Off92
module Offset9 (
  input  [15:0] IR,
  output [15:0] Off9
);

  assign Off9 = {{7{IR[8]}}, IR[8:0]};  // Bit_Extender bit_extender_1
endmodule

module Or16 (
  input  [15:0] in_1,
  output out_2
);

  wire [3:0] or_1_out;

  assign or_1_out = in_1[3:0] | in_1[7:4] | in_1[11:8] | in_1[15:12];  // OR_Gate or_1, 4 bits wide
  or or_2 (out_2, or_1_out[0], or_1_out[1], or_1_out[2], or_1_out[3]);
endmodule

module RamCtrl (
  input  Exec,
  input  Fetch,
  input  Load,
  input  Store,
  output MemLoad,
  output MemStore
);

  or or_1 (MemLoad, Fetch, Load);
  and and_1 (MemStore, Exec, Store);
endmodule

module Registres (
  input  [2:0] SR1,
  input  [15:0] IN,
  input  [2:0] SR2,
  input  WriteReg,
  input  [2:0] DR_SR,
  output [15:0] R0,
  output [15:0] OUT_SR1,
  output [15:0] R1,
  output [15:0] R2,
  output [15:0] R3,
  output [15:0] OUT_SR2,
  output [15:0] R4,
  output [15:0] R5,
  output [15:0] OUT_SR,
  output [15:0] R6,
  output [15:0] R7
);

  wire decoder_1_out0, decoder_1_out1, decoder_1_out2, decoder_1_out3, decoder_1_out4, decoder_1_out5,
       decoder_1_out6, decoder_1_out7;

  Decoder #(.select(3), .disabled(0)) decoder_1 (
    .out0(decoder_1_out0), .out1(decoder_1_out1), .out2(decoder_1_out2), .out3(decoder_1_out3),
    .out4(decoder_1_out4), .out5(decoder_1_out5), .out6(decoder_1_out6), .out7(decoder_1_out7), .sel(DR_SR),
    .en(WriteReg));
  Register #(.width(16), .trigger("falling")) u_R0 (.D(IN), .Q(R0), .clk(decoder_1_out0));  // open: en, clr
  Register #(.width(16), .trigger("falling")) u_R1 (.D(IN), .Q(R1), .clk(decoder_1_out1));  // open: en, clr
  Register #(.width(16), .trigger("falling")) u_R2 (.D(IN), .Q(R2), .clk(decoder_1_out2));  // open: en, clr
  Register #(.width(16), .trigger("falling")) u_R3 (.D(IN), .Q(R3), .clk(decoder_1_out3));  // open: en, clr
  Register #(.width(16), .trigger("falling")) u_R4 (.D(IN), .Q(R4), .clk(decoder_1_out4));  // open: en, clr
  Register #(.width(16), .trigger("falling")) u_R5 (.D(IN), .Q(R5), .clk(decoder_1_out5));  // open: en, clr
  Register #(.width(16), .trigger("falling")) u_R6 (.D(IN), .Q(R6), .clk(decoder_1_out6));  // open: en, clr
  Register #(.width(16), .trigger("falling")) u_R7 (.D(IN), .Q(R7), .clk(decoder_1_out7));  // open: en, clr
  Multiplexer #(.select(3), .width(16), .enable("false")) multiplexer_1 (
    .in0(R0), .in1(R1), .in2(R2), .in3(R3), .in4(R4), .in5(R5), .in6(R6), .in7(R7), .out(OUT_SR1), .sel(SR1));
  Multiplexer #(.select(3), .width(16), .enable("false")) multiplexer_2 (
    .in0(R0), .in1(R1), .in2(R2), .in3(R3), .in4(R4), .in5(R5), .in6(R6), .in7(R7), .out(OUT_SR2), .sel(SR2));
  Multiplexer #(.select(3), .width(16), .enable("false")) multiplexer_3 (
    .in0(R0), .in1(R1), .in2(R2), .in3(R3), .in4(R4), .in5(R5), .in6(R6), .in7(R7), .out(OUT_SR), .sel(DR_SR));
endmodule

module RegPC (
  input  [15:0] R,
  input  TestNZP,
  input  Jump,
  input  [15:0] IR,
  input  H,
  input  Reset,
  output [15:0] PC
);

  wire and_1_out, decodeop_1_br, decodeop_1_jmp, decodeop_1_jsr, decodeop_1_jsrr, or_1_out;
  wire [15:0] adder_1_out, bit_extender_1_out, bit_extender_2_out, multiplexer_1_out, multiplexer_2_out,
       multiplexer_3_out, multiplexer_4_out;

  assign bit_extender_1_out = {{7{IR[8]}}, IR[8:0]};  // Bit_Extender bit_extender_1
  assign bit_extender_2_out = {{5{IR[10]}}, IR[10:0]};  // Bit_Extender bit_extender_2
  DecodeOp decodeop_1 (
    .in_1(IR), .BR(decodeop_1_br), .JMP(decodeop_1_jmp), .JSR(decodeop_1_jsr), .JSRR(decodeop_1_jsrr));  // open: NOT, AND, ADD, LEA, ST, STR, STI, LD, LDR, LDI
  Multiplexer #(.width(16), .enable("false")) multiplexer_1 (
    .in0({16{1'b0}}), .in1(bit_extender_1_out), .out(multiplexer_1_out), .sel(and_1_out));
  and and_1 (and_1_out, TestNZP, decodeop_1_br);
  or or_1 (or_1_out, decodeop_1_jsrr, decodeop_1_jmp);
  Multiplexer #(.width(16), .enable("false")) multiplexer_2 (
    .in0(multiplexer_1_out), .in1(bit_extender_2_out), .out(multiplexer_2_out), .sel(decodeop_1_jsr));
  Multiplexer #(.width(16), .enable("false")) multiplexer_3 (
    .in0({16{1'b0}}), .in1(multiplexer_2_out), .out(multiplexer_3_out), .sel(Jump));
  Adder #(.width(16)) adder_1 (.a(PC), .b(multiplexer_3_out), .out(adder_1_out), .cin(1'b1));  // open: cout
  Multiplexer #(.width(16), .enable("false")) multiplexer_4 (
    .in0(adder_1_out), .in1(R), .out(multiplexer_4_out), .sel(or_1_out));
  Register #(.width(16), .trigger("falling")) u_PC (.D(multiplexer_4_out), .Q(PC), .clk(H), .clr(Reset));  // open: en

  // Notes on the sheet:
  //   PC <- PC + 1
endmodule

module CI (
  input  [15:0] PC,
  input  [15:0] MemOut,
  output DoLEA,
  output [15:0] out_4
);

  wire [15:0] offset9_1_off9;

  // DecodeOp decodeop_1: pin names not known; wires that end beside it: MemOut, DoLEA
  Offset9 offset9_1 (.IR(MemOut), .Off9(offset9_1_off9));
  // Probe on offset9_1_off9
  Adder #(.width(16)) adder_1 (.a(PC), .b(offset9_1_off9), .out(out_4), .cin(1'b1));  // open: cout
endmodule

module DecodeOp (
  input  [15:0] in_1,
  output NOT,
  output AND,
  output ADD,
  output LEA,
  output ST,
  output STR,
  output STI,
  output LD,
  output LDR,
  output LDI,
  output BR,
  output JMP,
  output JSR,
  output JSRR
);

  wire decoder_1_out4, not_1_out;

  Decoder #(.select(4), .enable("false")) decoder_1 (
    .out0(BR), .out1(ADD), .out2(LD), .out3(ST), .out4(decoder_1_out4), .out5(AND), .out6(LDR), .out7(STR),
    .out9(NOT), .out10(LDI), .out11(STI), .out12(JMP), .out14(LEA), .sel(in_1[15:12]));  // open: out8, out13, out15
  and and_1 (JSR, decoder_1_out4, in_1[11]);
  not not_1 (not_1_out, in_1[11]);
  and and_2 (JSRR, not_1_out, decoder_1_out4);
endmodule

module GetOp (
  input  [15:0] in_1,
  output [1:0] out_2
);

  wire decodeop_1_jsr, decodeop_1_jsrr, decodeop_1_lea, or_1_out;

  DecodeOp decodeop_1 (
    .in_1(in_1), .LEA(decodeop_1_lea), .JSR(decodeop_1_jsr), .JSRR(decodeop_1_jsrr));  // open: NOT, AND, ADD, ST, STR, STI, LD, LDR, LDI, BR, JMP
  or or_1 (or_1_out, decodeop_1_lea, decodeop_1_jsr, decodeop_1_jsrr);
  Multiplexer #(.width(2), .enable("false")) multiplexer_1 (
    .in0(in_1[15:14]), .in1(2'b00), .out(out_2), .sel(or_1_out));
endmodule

module Arg (
  input  [15:0] ARG1,
  input  [15:0] ARG2,
  input  [15:0] PC,
  input  [15:0] IR,
  output [15:0] out_5,
  output [15:0] out_6
);

  wire decodeop_1_jsr, decodeop_1_jsrr, decodeop_1_lea, or_1_out, or_2_out;
  wire [15:0] adder_1_out, bit_extender_1_out, multiplexer_3_out;

  DecodeOp decodeop_1 (
    .in_1(IR), .LEA(decodeop_1_lea), .JSR(decodeop_1_jsr), .JSRR(decodeop_1_jsrr));  // open: NOT, AND, ADD, ST, STR, STI, LD, LDR, LDI, BR, JMP
  assign bit_extender_1_out = {{7{IR[8]}}, IR[8:0]};  // Bit_Extender bit_extender_1
  Adder #(.width(16)) adder_1 (.a(PC), .b(16'h1), .out(adder_1_out));  // open: cin, cout
  or or_1 (or_1_out, decodeop_1_lea, decodeop_1_jsr, decodeop_1_jsrr);
  or or_2 (or_2_out, decodeop_1_jsr, decodeop_1_jsrr);
  Multiplexer #(.width(16), .enable("false")) multiplexer_1 (
    .in0(ARG1), .in1(adder_1_out), .out(out_5), .sel(or_1_out));
  Multiplexer #(.width(16), .enable("false")) multiplexer_2 (
    .in0(ARG2), .in1(multiplexer_3_out), .out(out_6), .sel(or_1_out));
  Multiplexer #(.width(16), .enable("false")) multiplexer_3 (
    .in0(bit_extender_1_out), .in1({16{1'b0}}), .out(multiplexer_3_out), .sel(or_2_out));
endmodule

module RegIn (
  input  [2:0] in_1,
  input  [15:0] in_2,
  output [2:0] out_3
);

  wire decodeop_1_jsr, decodeop_1_jsrr, or_1_out;

  DecodeOp decodeop_1 (
    .in_1(in_2), .JSR(decodeop_1_jsr), .JSRR(decodeop_1_jsrr));  // open: NOT, AND, ADD, LEA, ST, STR, STI, LD, LDR, LDI, BR, JMP
  or or_1 (or_1_out, decodeop_1_jsr, decodeop_1_jsrr);
  Multiplexer #(.width(3), .enable("false")) multiplexer_1 (.in0(in_1), .in1(3'b111), .out(out_3), .sel(or_1_out));
endmodule

module Xor (
  input  A0,
  input  B0,
  input  A1,
  input  B1,
  input  A2,
  input  B2,
  input  A3,
  input  B3,
  input  A4,
  input  B4,
  input  A5,
  input  B5,
  input  A6,
  input  B6,
  input  A7,
  input  B7,
  input  A8,
  input  B8,
  input  A9,
  input  B9,
  input  A10,
  input  B10,
  input  A11,
  input  B11,
  input  A12,
  input  B12,
  input  A13,
  input  B13,
  input  A14,
  input  B14,
  input  A15,
  input  B15,
  output S0,
  output S1,
  output S2,
  output S3,
  output S4,
  output S5,
  output S6,
  output S7,
  output S8,
  output S9,
  output S10,
  output S11,
  output S12,
  output S13,
  output S14,
  output S15
);

  xor xor_1 (S0, A0, B0);
  xor xor_2 (S1, A1, B1);
  xor xor_3 (S2, A2, B2);
  xor xor_4 (S3, A3, B3);
  xor xor_5 (S4, A4, B4);
  xor xor_6 (S5, A5, B5);
  xor xor_7 (S6, A6, B6);
  xor xor_8 (S7, A7, B7);
  xor xor_9 (S8, A8, B8);
  xor xor_10 (S9, A9, B9);
  xor xor_11 (S10, A10, B10);
  xor xor_12 (S11, A11, B11);
  xor xor_13 (S12, A12, B12);
  xor xor_14 (S13, A13, B13);
  xor xor_15 (S14, A14, B14);
  xor xor_16 (S15, A15, B15);
endmodule

module XXor (
  input  [15:0] B,
  input  [15:0] A,
  output [15:0] out_3
);

  Xor xor_1 (
    .A0(A[0]), .B0(B[0]), .A1(A[1]), .B1(B[1]), .A2(A[2]), .B2(B[2]), .A3(A[3]), .B3(B[3]), .A4(A[4]),
    .B4(B[4]), .A5(A[5]), .B5(B[5]), .A6(A[6]), .B6(B[6]), .A7(A[7]), .B7(B[7]), .A8(A[8]), .B8(B[8]),
    .A9(A[9]), .B9(B[9]), .A10(A[10]), .B10(B[10]), .A11(A[11]), .B11(B[11]), .A12(A[12]), .B12(B[12]),
    .A13(A[13]), .B13(B[13]), .A14(A[14]), .B14(B[14]), .A15(A[15]), .B15(B[15]), .S0(out_3[0]),
    .S1(out_3[1]), .S2(out_3[2]), .S3(out_3[3]), .S4(out_3[4]), .S5(out_3[5]), .S6(out_3[6]), .S7(out_3[7]),
    .S8(out_3[8]), .S9(out_3[9]), .S10(out_3[10]), .S11(out_3[11]), .S12(out_3[12]), .S13(out_3[13]),
    .S14(out_3[14]), .S15(out_3[15]));
endmodule

module OAddr (
  input  [15:0] Addr1,
  input  [15:0] Addr2,
  output [15:0] out_3,
  output In
);

  Multiplexer #(.width(16), .enable("false")) multiplexer_1 (.in0(Addr1), .in1(Addr2), .out(out_3), .sel(In));
endmodule
